// Logisim project 1 4 bit full adder.circ as structural Verilog: 1 circuit, main circuit main
module main (
  input  [3:0] A0,
  input  Cin,
  input  [3:0] B0,
  output Cout,
  output [3:0] S0
);

  Adder #(.width(4)) adder_1 (.a(A0), .b(B0), .out(S0), .cin(Cin), .cout(Cout));
endmodule
