// Logisim project 1 bit full Adder.circ as structural Verilog: 1 circuit, main circuit main
module main (
  input  A,
  input  B,
  input  C,
  output out_4,
  output out_5
);

  wire A_B_out, AB_out, ACin_out, BCin_out, or_1_out;

  xor A_B (A_B_out, A, B);
  and AB (AB_out, A, B);
  and BCin (BCin_out, B, C);
  and ACin (ACin_out, A, C);
  or or_1 (or_1_out, AB_out, BCin_out);
  xor Sum (out_4, A_B_out, C);
  or Cout (out_5, or_1_out, ACin_out);
endmodule
