// Logisim project 2 2 bit full adder.circ as structural Verilog: 1 circuit, main circuit main
module main (
  input  [1:0] A1,
  input  [1:0] A0,
  input  Cin,
  input  [1:0] B1,
  input  [1:0] B0,
  output Cout,
  output [1:0] S1,
  output [1:0] S0
);

  wire adder_1_cout;

  Adder #(.width(2)) adder_1 (.a(A0), .b(B0), .out(S0), .cin(Cin), .cout(adder_1_cout));
  Adder #(.width(2)) adder_2 (.a(A1), .b(B1), .out(S1), .cin(adder_1_cout), .cout(Cout));
endmodule
