// Logisim project 3 to 8 Active High Decoder with default circuit.circ as structural Verilog: 1 circuit, main circuit main
module main (
  input  [1:0] I1_I0,
  input  En,
  output out_3
);

  wire decoder_1_out0, decoder_1_out1, decoder_1_out2, decoder_1_out3, decoder_2_out0, decoder_2_out1,
       decoder_2_out2, decoder_2_out3, not_1_out, or_1_out, or_2_out;

  not not_1 (not_1_out, En);
  Decoder #(.select(2)) decoder_1 (
    .out0(decoder_1_out0), .out1(decoder_1_out1), .out2(decoder_1_out2), .out3(decoder_1_out3), .sel(I1_I0),
    .en(En));
  Decoder #(.select(2)) decoder_2 (
    .out0(decoder_2_out0), .out1(decoder_2_out1), .out2(decoder_2_out2), .out3(decoder_2_out3), .sel(I1_I0),
    .en(not_1_out));
  or or_1 (or_1_out, decoder_1_out0, decoder_2_out0);
  or or_2 (or_2_out, decoder_2_out1, decoder_2_out3);
  or or_3 (out_3, or_1_out, or_2_out);

  // Notes on the sheet:
  //   m0
  //   m4
  //   m5
  //   m7
  //   F = m0 + m4 + m5 + m7
endmodule
