// Logisim project 3 to 8 Active High Decoder.circ as structural Verilog: 2 circuits, main circuit main
module main (
  input  Enable,
  input  I2,
  input  I1,
  input  I0
);

  wire n3_to_8_active_high_decoder_1_d0, n3_to_8_active_high_decoder_1_d1, n3_to_8_active_high_decoder_1_d2,
       n3_to_8_active_high_decoder_1_d3, n3_to_8_active_high_decoder_1_d4, n3_to_8_active_high_decoder_1_d5,
       n3_to_8_active_high_decoder_1_d6, n3_to_8_active_high_decoder_1_d7;

  _3_to_8_Active_High_Decoder u_3_to_8_active_high_decoder_1 (
    .in_1(Enable), .I2(I2), .I1(I1), .I0(I0), .D0(n3_to_8_active_high_decoder_1_d0),
    .D1(n3_to_8_active_high_decoder_1_d1), .D2(n3_to_8_active_high_decoder_1_d2),
    .D3(n3_to_8_active_high_decoder_1_d3), .D4(n3_to_8_active_high_decoder_1_d4),
    .D5(n3_to_8_active_high_decoder_1_d5), .D6(n3_to_8_active_high_decoder_1_d6),
    .D7(n3_to_8_active_high_decoder_1_d7));
  LED D7 (.in(n3_to_8_active_high_decoder_1_d7));
  LED D5 (.in(n3_to_8_active_high_decoder_1_d5));
  LED D6 (.in(n3_to_8_active_high_decoder_1_d6));
  LED D4 (.in(n3_to_8_active_high_decoder_1_d4));
  LED D2 (.in(n3_to_8_active_high_decoder_1_d2));
  LED D3 (.in(n3_to_8_active_high_decoder_1_d3));
  LED D0 (.in(n3_to_8_active_high_decoder_1_d0));
  LED D1 (.in(n3_to_8_active_high_decoder_1_d1));
endmodule

module _3_to_8_Active_High_Decoder (
  input  in_1,
  input  I2,
  input  I1,
  input  I0,
  output D0,
  output D1,
  output D2,
  output D3,
  output D4,
  output D5,
  output D6,
  output D7
);

  wire and_1_out, and_2_out, and_3_out, and_4_out, and_5_out, and_6_out, and_7_out, and_8_out, and_9_out,
       and_10_out, and_11_out, and_12_out, and_13_out, and_14_out, and_15_out, and_16_out, I0_prime_out,
       I1_prime_out, I2_prime_out;

  not I2_prime (I2_prime_out, I2);
  not I1_prime (I1_prime_out, I1);
  not I0_prime (I0_prime_out, I0);
  and and_1 (and_1_out, I2_prime_out, I1_prime_out);
  and and_2 (and_2_out, I2_prime_out, I1_prime_out);
  and and_3 (and_3_out, I2_prime_out, I1);
  and and_4 (and_4_out, I2_prime_out, I1);
  and and_5 (and_5_out, I2, I1_prime_out);
  and and_6 (and_6_out, I2, I1_prime_out);
  and and_7 (and_7_out, I2, I1);
  and and_8 (and_8_out, I2, I1);
  and and_9 (and_9_out, and_1_out, I0_prime_out);
  and and_10 (and_10_out, and_2_out, I0);
  and and_11 (and_11_out, and_3_out, I0_prime_out);
  and and_12 (and_12_out, and_4_out, I0);
  and and_13 (and_13_out, and_5_out, I0_prime_out);
  and and_14 (and_14_out, and_6_out, I0);
  and and_15 (and_15_out, and_7_out, I0_prime_out);
  and and_16 (and_16_out, and_8_out, I0);
  and and_17 (D0, and_9_out, in_1);
  and and_18 (D1, and_10_out, in_1);
  and and_19 (D2, and_11_out, in_1);
  and and_20 (D3, and_12_out, in_1);
  and and_21 (D4, and_13_out, in_1);
  and and_22 (D5, and_14_out, in_1);
  and and_23 (D6, and_15_out, in_1);
  and and_24 (D7, and_16_out, in_1);

  // Notes on the sheet:
  //   3 to 8 Active High Decoder Circuit
endmodule
