// Logisim project 3 to 8 Active Low Decoder with default circuit.circ as structural Verilog: 1 circuit, main circuit main
module main (
  input  [1:0] I1_I0,
  input  En
);

  wire decoder_1_out0, decoder_1_out1, decoder_1_out2, decoder_1_out3, decoder_2_out0, decoder_2_out1,
       decoder_2_out2, decoder_2_out3, not_1_out, not_2_out, not_3_out, not_4_out, not_5_out, not_6_out,
       not_7_out, not_8_out, not_9_out;

  not not_1 (not_1_out, En);
  Decoder #(.select(2)) decoder_1 (
    .out0(decoder_1_out0), .out1(decoder_1_out1), .out2(decoder_1_out2), .out3(decoder_1_out3), .sel(I1_I0),
    .en(not_1_out));
  Decoder #(.select(2)) decoder_2 (
    .out0(decoder_2_out0), .out1(decoder_2_out1), .out2(decoder_2_out2), .out3(decoder_2_out3), .sel(I1_I0),
    .en(En));
  not not_2 (not_2_out, decoder_1_out0);
  not not_3 (not_3_out, decoder_1_out1);
  not not_4 (not_4_out, decoder_1_out2);
  not not_5 (not_5_out, decoder_1_out3);
  not not_6 (not_6_out, decoder_2_out0);
  not not_7 (not_7_out, decoder_2_out1);
  not not_8 (not_8_out, decoder_2_out2);
  not not_9 (not_9_out, decoder_2_out3);
  LED D0 (.in(not_2_out));
  LED D1 (.in(not_3_out));
  LED D2 (.in(not_4_out));
  LED D3 (.in(not_5_out));
  LED D4 (.in(not_6_out));
  LED D5 (.in(not_7_out));
  LED D6 (.in(not_8_out));
  LED D7 (.in(not_9_out));
endmodule
