// Logisim project 3 to 8 Active Low Decoder.circ as structural Verilog: 2 circuits, main circuit main
// Enable
module main (
  input  Enable,
  input  I2,
  input  I1,
  input  I0
);

  wire n3_to_8_active_low_decoder_1_d0, n3_to_8_active_low_decoder_1_d1, n3_to_8_active_low_decoder_1_d2,
       n3_to_8_active_low_decoder_1_d3, n3_to_8_active_low_decoder_1_d4, n3_to_8_active_low_decoder_1_d5,
       n3_to_8_active_low_decoder_1_d6, n3_to_8_active_low_decoder_1_d7;

  _3_to_8_Active_Low_Decoder u_3_to_8_active_low_decoder_1 (
    .in_1(Enable), .I2(I2), .I1(I1), .I0(I0), .D0(n3_to_8_active_low_decoder_1_d0),
    .D1(n3_to_8_active_low_decoder_1_d1), .D2(n3_to_8_active_low_decoder_1_d2),
    .D3(n3_to_8_active_low_decoder_1_d3), .D4(n3_to_8_active_low_decoder_1_d4),
    .D5(n3_to_8_active_low_decoder_1_d5), .D6(n3_to_8_active_low_decoder_1_d6),
    .D7(n3_to_8_active_low_decoder_1_d7));
  LED D7 (.in(n3_to_8_active_low_decoder_1_d7));
  LED D5 (.in(n3_to_8_active_low_decoder_1_d5));
  LED D6 (.in(n3_to_8_active_low_decoder_1_d6));
  LED D4 (.in(n3_to_8_active_low_decoder_1_d4));
  LED D3 (.in(n3_to_8_active_low_decoder_1_d3));
  LED D2 (.in(n3_to_8_active_low_decoder_1_d2));
  LED D1 (.in(n3_to_8_active_low_decoder_1_d1));
  LED D0 (.in(n3_to_8_active_low_decoder_1_d0));
endmodule

module _3_to_8_Active_Low_Decoder (
  input  in_1,
  input  I2,
  input  I1,
  input  I0,
  output D0,
  output D1,
  output D2,
  output D3,
  output D4,
  output D5,
  output D6,
  output D7
);

  wire and_1_out, and_2_out, and_3_out, and_4_out, and_5_out, and_6_out, and_7_out, and_8_out, and_9_out,
       and_10_out, and_11_out, and_12_out, and_13_out, and_14_out, and_15_out, and_16_out, I0_prime_out,
       I1_prime_out, I2_prime_out, not_1_out, not_2_out, not_3_out, not_4_out, not_5_out, not_6_out,
       not_7_out, not_8_out, not_9_out;

  not not_1 (not_1_out, in_1);
  not I2_prime (I2_prime_out, I2);
  not I1_prime (I1_prime_out, I1);
  not I0_prime (I0_prime_out, I0);
  and and_1 (and_1_out, I2_prime_out, I1_prime_out);
  and and_2 (and_2_out, I2_prime_out, I1_prime_out);
  and and_3 (and_3_out, I2_prime_out, I1);
  and and_4 (and_4_out, I2_prime_out, I1);
  and and_5 (and_5_out, I2, I1_prime_out);
  and and_6 (and_6_out, I2, I1_prime_out);
  and and_7 (and_7_out, I2, I1);
  and and_8 (and_8_out, I2, I1);
  and and_9 (and_9_out, and_1_out, I0_prime_out);
  and and_10 (and_10_out, and_2_out, I0);
  and and_11 (and_11_out, and_3_out, I0_prime_out);
  and and_12 (and_12_out, and_4_out, I0);
  and and_13 (and_13_out, and_5_out, I0_prime_out);
  and and_14 (and_14_out, and_6_out, I0);
  and and_15 (and_15_out, and_7_out, I0_prime_out);
  and and_16 (and_16_out, and_8_out, I0);
  not not_2 (not_2_out, and_9_out);
  not not_3 (not_3_out, and_10_out);
  not not_4 (not_4_out, and_11_out);
  not not_5 (not_5_out, and_12_out);
  not not_6 (not_6_out, and_13_out);
  not not_7 (not_7_out, and_14_out);
  not not_8 (not_8_out, and_15_out);
  not not_9 (not_9_out, and_16_out);
  and and_17 (D0, not_2_out, not_1_out);
  and and_18 (D1, not_3_out, not_1_out);
  and and_19 (D2, not_4_out, not_1_out);
  and and_20 (D3, not_5_out, not_1_out);
  and and_21 (D4, not_6_out, not_1_out);
  and and_22 (D5, not_7_out, not_1_out);
  and and_23 (D6, not_8_out, not_1_out);
  and and_24 (D7, not_9_out, not_1_out);

  // Notes on the sheet:
  //   3 to 8 Active Low Decoder Circuit
endmodule
