// Logisim project 3-bit register with D flip flop.circ as structural Verilog: 1 circuit, main circuit main
module main (
  input  in_1,
  input  in_2,
  input  in_3,
  output out_4,
  output out_5,
  output out_6
);

  wire clock_1_out;

  Clock clock_1 (.out(clock_1_out));
  D_Flip_Flop d_ff_1 (.clk(clock_1_out), .D(in_3), .Q(out_4));  // open: Qn, preset, en, reset
  D_Flip_Flop d_ff_2 (.clk(clock_1_out), .D(in_2), .Q(out_5));  // open: Qn, preset, en, reset
  D_Flip_Flop d_ff_3 (.clk(clock_1_out), .D(in_1), .Q(out_6));  // open: Qn, preset, en, reset
  // Probe on {out_6, out_5, out_4}

  // Notes on the sheet:
  //   3-bit register from inbuilt D Flip Flop
endmodule
