// Logisim project 3-bit register with the logic circuit of D Flip Flop.circ as structural Verilog: 2 circuits, main circuit main
module main (
  input  in_1,
  input  in_2,
  input  in_3,
  output out_4,
  output out_5,
  output out_6
);

  wire clock_1_out;

  D_flip_flop_Main_Circuit d_flip_flop_main_circuit_1 (.Clock(clock_1_out), .D(in_3), .Q(out_4));  // open: Q_prime
  D_flip_flop_Main_Circuit d_flip_flop_main_circuit_2 (.Clock(clock_1_out), .D(in_2), .Q(out_5));  // open: Q_prime
  D_flip_flop_Main_Circuit d_flip_flop_main_circuit_3 (.Clock(clock_1_out), .D(in_1), .Q(out_6));  // open: Q_prime
  Clock clock_1 (.out(clock_1_out));
  // Probe on {out_6, out_5, out_4}

  // Notes on the sheet:
  //   3 bit Register from D Flip Flop Circuit
endmodule

module D_flip_flop_Main_Circuit (
  input  Clock,
  input  D,
  output Q,
  output Q_prime
);

  wire and_1_out, and_2_out, not_1_out;

  not not_1 (not_1_out, D);
  and and_1 (and_1_out, not_1_out, Clock);
  and and_2 (and_2_out, Clock, D);
  nor nor_1 (Q, and_1_out, Q_prime);
  nor nor_2 (Q_prime, Q, and_2_out);
endmodule
