// Logisim project 4 1 bit full adder.circ as structural Verilog: 2 circuits, main circuit main
module main (
  input  A3,
  input  A2,
  input  A1,
  input  A0,
  input  C_in,
  input  B3,
  input  B2,
  input  B1,
  input  B0,
  output C_out,
  output S3,
  output S2,
  output S1,
  output S0
);

  wire n1_bit_full_adder_1_out_5, n1_bit_full_adder_2_out_5, n1_bit_full_adder_3_out_5;

  _1_bit_full_adder u_1_bit_full_adder_1 (.A(A0), .B(B0), .C_IN(C_in), .out_4(S0), .out_5(n1_bit_full_adder_1_out_5));
  _1_bit_full_adder u_1_bit_full_adder_2 (
    .A(A1), .B(B1), .C_IN(n1_bit_full_adder_1_out_5), .out_4(S1), .out_5(n1_bit_full_adder_2_out_5));
  _1_bit_full_adder u_1_bit_full_adder_3 (
    .A(A2), .B(B2), .C_IN(n1_bit_full_adder_2_out_5), .out_4(S2), .out_5(n1_bit_full_adder_3_out_5));
  _1_bit_full_adder u_1_bit_full_adder_4 (.A(A3), .B(B3), .C_IN(n1_bit_full_adder_3_out_5), .out_4(S3), .out_5(C_out));
endmodule

module _1_bit_full_adder (
  input  A,
  input  B,
  input  C_IN,
  output out_4,
  output out_5
);

  wire A_B_out, AB_out, ACin_out, BCin_out, or_1_out;

  xor A_B (A_B_out, A, B);
  and AB (AB_out, A, B);
  and BCin (BCin_out, B, C_IN);
  and ACin (ACin_out, A, C_IN);
  or or_1 (or_1_out, AB_out, BCin_out);
  xor Sum (out_4, A_B_out, C_IN);
  or Cout (out_5, or_1_out, ACin_out);
endmodule
