// Logisim project 4 to 1 MUX.circ as structural Verilog: 1 circuit, main circuit main
module main (
  input  [1:0] A_B,
  input  C,
  output out_3
);

  wire C_prime_out;

  not C_prime (C_prime_out, C);
  Multiplexer #(.select(2), .disabled(0), .enable("false")) multiplexer_1 (
    .in0(C), .in1(C), .in2(C_prime_out), .in3(C_prime_out), .out(out_3), .sel(A_B));

  // Notes on the sheet:
  //   F(A,B,C) = ∑m (1, 3, 4, 6)
endmodule
