// Logisim project Arbitary Counter.circ as structural Verilog: 1 circuit, main circuit main
module main (
);

  wire and_1_out, and_2_out, clock_1_out, j_k_ff_1_qn, j_k_ff_2_qn, j_k_ff_3_qn, or_1_out, or_2_out, or_3_out;
  wire [2:0] j_k_ff_1_q;

  and and_1 (and_1_out, j_k_ff_3_qn, j_k_ff_1_q[1]);
  or or_1 (or_1_out, j_k_ff_1_q[2], j_k_ff_2_qn);
  or or_2 (or_2_out, j_k_ff_1_q[0], j_k_ff_1_q[2]);
  and and_2 (and_2_out, j_k_ff_1_q[0], j_k_ff_2_qn);
  or or_3 (or_3_out, j_k_ff_1_q[1], j_k_ff_1_q[0]);
  Clock clock_1 (.out(clock_1_out));
  J_K_Flip_Flop j_k_ff_1 (
    .J(and_1_out), .clk(clock_1_out), .K(or_1_out), .Q(j_k_ff_1_q[0]), .Qn(j_k_ff_1_qn));  // open: preset, en, reset
  J_K_Flip_Flop j_k_ff_2 (
    .J(j_k_ff_1_qn), .clk(clock_1_out), .K(or_2_out), .Q(j_k_ff_1_q[1]), .Qn(j_k_ff_2_qn));  // open: preset, en, reset
  J_K_Flip_Flop j_k_ff_3 (
    .J(and_2_out), .clk(clock_1_out), .K(or_3_out), .Q(j_k_ff_1_q[2]), .Qn(j_k_ff_3_qn));  // open: preset, en, reset
  // Probe on j_k_ff_1_q

  // Notes on the sheet:
  //   Q2
  //   Q2'
  //   Q1
  //   Q0'
  //   Q1'
  //   Q0
  //   JK0
  //   JK1
  //   JK2
endmodule
