// Logisim project Counter.circ as structural Verilog: 1 circuit, main circuit main
module main (
  input  in_1,
  input  in_2,
  input  in_3,
  input  in_4
);

  wire clock_1_out, clock_2_out, clock_3_out, clock_4_out, j_k_ff_2_qn, j_k_ff_6_qn;
  wire [1:0] j_k_ff_2_q, j_k_ff_4_q, j_k_ff_6_q, j_k_ff_8_q;

  Clock clock_1 (.out(clock_1_out));
  Clock clock_2 (.out(clock_2_out));
  J_K_Flip_Flop #(.trigger("falling")) j_k_ff_1 (
    .J(in_1), .clk(j_k_ff_2_qn), .K(in_1), .Q(j_k_ff_2_q[1]));  // open: Qn, preset, en, reset
  J_K_Flip_Flop #(.trigger("falling")) j_k_ff_2 (
    .J(in_1), .clk(clock_1_out), .K(in_1), .Q(j_k_ff_2_q[0]), .Qn(j_k_ff_2_qn));  // open: preset, en, reset
  J_K_Flip_Flop j_k_ff_3 (.J(in_4), .clk(j_k_ff_4_q[0]), .K(in_4), .Q(j_k_ff_4_q[1]));  // open: Qn, preset, en, reset
  J_K_Flip_Flop j_k_ff_4 (.J(in_4), .clk(clock_2_out), .K(in_4), .Q(j_k_ff_4_q[0]));  // open: Qn, preset, en, reset
  // Probe on j_k_ff_2_q
  // Probe on j_k_ff_4_q
  Clock clock_3 (.out(clock_3_out));
  Clock clock_4 (.out(clock_4_out));
  J_K_Flip_Flop j_k_ff_5 (.J(in_2), .clk(j_k_ff_6_qn), .K(in_2), .Q(j_k_ff_6_q[1]));  // open: Qn, preset, en, reset
  J_K_Flip_Flop j_k_ff_6 (
    .J(in_2), .clk(clock_3_out), .K(in_2), .Q(j_k_ff_6_q[0]), .Qn(j_k_ff_6_qn));  // open: preset, en, reset
  J_K_Flip_Flop #(.trigger("falling")) j_k_ff_7 (
    .J(in_3), .clk(j_k_ff_8_q[0]), .K(in_3), .Q(j_k_ff_8_q[1]));  // open: Qn, preset, en, reset
  J_K_Flip_Flop #(.trigger("falling")) j_k_ff_8 (
    .J(in_3), .clk(clock_4_out), .K(in_3), .Q(j_k_ff_8_q[0]));  // open: Qn, preset, en, reset
  // Probe on j_k_ff_6_q
  // Probe on j_k_ff_8_q

  // Notes on the sheet:
  //   Negative edge Down Counter
  //   Positive edge Down Counter
  //   Positive edge UP Counter
  //   Negative edge UP Counter
endmodule
