// Logisim project DAR2.circ as structural Verilog: 1 circuit, main circuit main
module main (
  input  A,
  input  B,
  input  C,
  input  D,
  output out_5
);

  wire A_C_out, A_prime_out, AC_out, AC_prime_D_out, and_1_out, B_prime_out, BD_prime_out, C_prime_out,
       D_prime_out;

  not A_prime (A_prime_out, A);
  not B_prime (B_prime_out, B);
  not C_prime (C_prime_out, C);
  not D_prime (D_prime_out, D);
  and AC_prime_D (AC_prime_D_out, A, C_prime_out, D);
  and AC (AC_out, A, C);
  and BD_prime (BD_prime_out, B, D_prime_out);
  or A_C (A_C_out, A, C);
  and and_1 (and_1_out, BD_prime_out, A_C_out);
  or or_1 (out_5, AC_prime_D_out, AC_out, and_1_out);
endmodule
