// Logisim project Draft circuit.circ as structural Verilog: 1 circuit, main circuit main
module main (
  input  A,
  input  B,
  input  C,
  input  D,
  output out_5
);

  wire A_C_out, A_C_prime_D_C_out, A_prime_out, B_prime_out, BD_prime_A_C_out, BD_prime_out, C_prime_D_C_out,
       C_prime_D_out, C_prime_out, D_prime_out;

  not A_prime (A_prime_out, A);
  not B_prime (B_prime_out, B);
  not C_prime (C_prime_out, C);
  not D_prime (D_prime_out, D);
  and C_prime_D (C_prime_D_out, C_prime_out, D_prime_out);
  and BD_prime (BD_prime_out, B, D_prime_out);
  or A_C (A_C_out, A, C);
  or C_prime_D_C (C_prime_D_C_out, C_prime_D_out, C);
  and BD_prime_A_C (BD_prime_A_C_out, BD_prime_out, A_C_out);
  and A_C_prime_D_C (A_C_prime_D_C_out, C_prime_D_C_out, A);
  or or_1 (out_5, A_C_prime_D_C_out, BD_prime_A_C_out);
endmodule
