// Logisim project F = M1 . M3 . M6 . M7  Active Low (POS) Decoder with Default Circuit.circ as structural Verilog: 1 circuit, main circuit main
module main (
  input  Enable,
  input  [2:0] I2__I1__I0,
  output out_3
);

  wire and_1_out, and_2_out, decoder_1_out0, decoder_1_out1, decoder_1_out2, decoder_1_out3, decoder_1_out4,
       decoder_1_out5, decoder_1_out6, decoder_1_out7, M1_out, M3_out, M6_out, M7_out, not_1_out;

  not not_1 (not_1_out, Enable);
  Decoder #(.select(3)) decoder_1 (
    .out0(decoder_1_out0), .out1(decoder_1_out1), .out2(decoder_1_out2), .out3(decoder_1_out3),
    .out4(decoder_1_out4), .out5(decoder_1_out5), .out6(decoder_1_out6), .out7(decoder_1_out7),
    .sel(I2__I1__I0), .en(not_1_out));
  not M1 (M1_out, decoder_1_out1);
  not M3 (M3_out, decoder_1_out3);
  not M6 (M6_out, decoder_1_out6);
  not M7 (M7_out, decoder_1_out7);
  and and_1 (and_1_out, M1_out, M3_out);
  and and_2 (and_2_out, M6_out, M7_out);
  and and_3 (out_3, and_1_out, and_2_out);
endmodule
