// Logisim project F = m0 + m4 + m5 + m7 Active High (SOP) Decoder{2 to 4 with 3 to 8} with Default Circuit.circ as structural Verilog: 1 circuit, main circuit main
module main (
);

  Decoder #(.select(2)) decoder_1 ();  // open: out0, out1, out2, out3, sel, en
  Decoder #(.select(2)) decoder_2 ();  // open: out0, out1, out2, out3, sel, en
endmodule
