// Logisim project F = m0 + m4 + m5 + m7 Active High (SOP) Decoder{2 to 4 with 3 to 8}.circ as structural Verilog: 2 circuits, main circuit main
module main (
  input  I2_Enable,
  input  I1,
  input  I0,
  output F___m0___m4___m5___m7
);

  wire n2_to4_with_3_to_8_1_d0, n2_to4_with_3_to_8_1_d1, n2_to4_with_3_to_8_1_d2, n2_to4_with_3_to_8_1_d3,
       n2_to4_with_3_to_8_1_d4, n2_to4_with_3_to_8_1_d5, n2_to4_with_3_to_8_1_d6, n2_to4_with_3_to_8_1_d7,
       or_1_out, or_2_out;

  _2_TO4_with_3_to_8 u_2_to4_with_3_to_8_1 (
    .I2_Enable(I2_Enable), .I1(I1), .I0(I0), .D0(n2_to4_with_3_to_8_1_d0), .D1(n2_to4_with_3_to_8_1_d1),
    .D2(n2_to4_with_3_to_8_1_d2), .D3(n2_to4_with_3_to_8_1_d3), .D4(n2_to4_with_3_to_8_1_d4),
    .D5(n2_to4_with_3_to_8_1_d5), .D6(n2_to4_with_3_to_8_1_d6), .D7(n2_to4_with_3_to_8_1_d7));
  or or_1 (or_1_out, n2_to4_with_3_to_8_1_d0, n2_to4_with_3_to_8_1_d4);
  or or_2 (or_2_out, n2_to4_with_3_to_8_1_d5, n2_to4_with_3_to_8_1_d7);
  or or_3 (F___m0___m4___m5___m7, or_1_out, or_2_out);

  // Notes on the sheet:
  //   M0
  //   M4
  //   M5
  //   M7
  //   3-to-8 line decoder  (the one we have designed with two 2-to-4 line decoders)
endmodule

module _2_TO4_with_3_to_8 (
  input  I2_Enable,
  input  I1,
  input  I0,
  output D0,
  output D1,
  output D2,
  output D3,
  output D4,
  output D5,
  output D6,
  output D7
);

  wire and_1_out, and_2_out, and_3_out, and_4_out, and_5_out, and_6_out, and_7_out, and_8_out, I0_prime_out,
       I1_prime_out, not_1_out;

  not I1_prime (I1_prime_out, I1);
  not not_1 (not_1_out, I2_Enable);
  not I0_prime (I0_prime_out, I0);
  and and_1 (and_1_out, I1_prime_out, I0_prime_out);
  and and_2 (and_2_out, I1_prime_out, I0);
  and and_3 (and_3_out, I1, I0_prime_out);
  and and_4 (and_4_out, I1, I0);
  and and_5 (and_5_out, I1_prime_out, I0_prime_out);
  and and_6 (and_6_out, I1_prime_out, I0);
  and and_7 (and_7_out, I1, I0_prime_out);
  and and_8 (and_8_out, I1, I0);
  and and_9 (D0, and_1_out, I2_Enable);
  and and_10 (D1, and_2_out, I2_Enable);
  and and_11 (D2, and_3_out, I2_Enable);
  and and_12 (D3, and_4_out, I2_Enable);
  and and_13 (D4, and_5_out, not_1_out);
  and and_14 (D5, and_6_out, not_1_out);
  and and_15 (D6, and_7_out, not_1_out);
  and and_16 (D7, and_8_out, not_1_out);

  // Notes on the sheet:
  //   3-to-8 line decoder Circuit  (the one we have designed with two 2-to-4 line decoders)
endmodule
