// Logisim project Jotil BORTONI.circ as structural Verilog: 1 circuit, main circuit main
module main (
  input  [1:0] in_1,
  input  in_2,
  input  in_3,
  input  in_4,
  input  in_5,
  input  in_6,
  input  in_7,
  output out_8,
  output out_9,
  output out_10,
  output out_11
);

  wire clock_1_out, multiplexer_1_out, multiplexer_2_out, multiplexer_3_out, multiplexer_4_out;

  Clock clock_1 (.out(clock_1_out));
  D_Flip_Flop d_ff_1 (.clk(clock_1_out), .D(multiplexer_1_out), .Q(out_8));  // open: Qn, preset, en, reset
  Multiplexer #(.select(2), .disabled(0), .enable("false")) multiplexer_1 (
    .in0(out_9), .in1(in_4), .in2(out_8), .in3(in_2), .out(multiplexer_1_out), .sel(in_1));
  D_Flip_Flop d_ff_2 (.clk(clock_1_out), .D(multiplexer_2_out), .Q(out_9));  // open: Qn, preset, en, reset
  Multiplexer #(.select(2), .disabled(0), .enable("false")) multiplexer_2 (
    .in0(out_10), .in1(in_5), .in2(out_9), .in3(out_8), .out(multiplexer_2_out), .sel(in_1));
  D_Flip_Flop d_ff_3 (.clk(clock_1_out), .D(multiplexer_3_out), .Q(out_10));  // open: Qn, preset, en, reset
  Multiplexer #(.select(2), .disabled(0), .enable("false")) multiplexer_3 (
    .in0(out_11), .in1(in_6), .in2(out_10), .in3(out_9), .out(multiplexer_3_out), .sel(in_1));
  D_Flip_Flop d_ff_4 (.clk(clock_1_out), .D(multiplexer_4_out), .Q(out_11));  // open: Qn, preset, en, reset
  Multiplexer #(.select(2), .disabled(0), .enable("false")) multiplexer_4 (
    .in0(in_3), .in1(in_7), .in2(out_11), .in3(out_10), .out(multiplexer_4_out), .sel(in_1));
endmodule
