// Logisim project L-01_report_QS-01.circ as structural Verilog: 1 circuit, main circuit main
module main (
  input  A,
  input  B,
  input  C,
  output out_4
);

  wire A_C_prime_out, A_prime_out, B_prime_out, C_prime_out;

  not A_prime (A_prime_out, A);
  not B_prime (B_prime_out, B);
  not C_prime (C_prime_out, C);
  or A_C_prime (A_C_prime_out, A, C_prime_out);
  and B_prime_A_C_prime (out_4, A_C_prime_out, B_prime_out);
endmodule
