// Logisim project L-01_report_QS-02.circ as structural Verilog: 1 circuit, main circuit main
module main (
  input  A,
  input  B,
  input  C,
  input  D,
  output out_5
);

  wire AB_AC_out, AB_out, AC_out, AD_prime_BCD_prime_out, AD_prime_out, BC_out, BCD_prime_out, D_prime_out;

  not D_prime (D_prime_out, D);
  and BC (BC_out, B, C);
  and AB (AB_out, A, B);
  and AC (AC_out, A, C);
  and AD_prime (AD_prime_out, A, D_prime_out);
  and BCD_prime (BCD_prime_out, BC_out, D_prime_out);
  or AB_AC (AB_AC_out, AB_out, AC_out);
  or AD_prime_BCD_prime (AD_prime_BCD_prime_out, AD_prime_out, BCD_prime_out);
  or or_1 (out_5, AB_AC_out, AD_prime_BCD_prime_out);
endmodule
