// Logisim project c zero one up down counter.circ as structural Verilog: 1 circuit, main circuit main
module main (
  input  in_1
);

  wire and_1_out, and_2_out, and_3_out, and_4_out, and_5_out, and_6_out, and_7_out, and_8_out, and_9_out,
       clock_1_out, d_ff_1_qn, d_ff_2_qn, d_ff_3_qn, not_1_out, or_1_out, or_2_out;
  wire [2:0] d_ff_3_q;

  not not_1 (not_1_out, in_1);
  and and_1 (and_1_out, d_ff_3_q[1], d_ff_3_qn, d_ff_3_q[2]);
  and and_2 (and_2_out, not_1_out, d_ff_3_q[2], d_ff_3_qn);
  and and_3 (and_3_out, in_1, d_ff_3_q[2], d_ff_2_qn);
  and and_4 (and_4_out, not_1_out, d_ff_1_qn, d_ff_2_qn, d_ff_3_qn);
  and and_5 (and_5_out, in_1, d_ff_1_qn, d_ff_3_q[1], d_ff_3_q[0]);
  and and_6 (and_6_out, in_1, d_ff_3_q[1], d_ff_3_qn);
  and and_7 (and_7_out, not_1_out, d_ff_3_q[1], d_ff_3_q[0]);
  and and_8 (and_8_out, not_1_out, d_ff_2_qn, d_ff_3_qn);
  and and_9 (and_9_out, in_1, d_ff_2_qn, d_ff_3_q[0]);
  or or_1 (or_1_out, and_6_out, and_7_out, and_8_out, and_9_out);
  or or_2 (or_2_out, and_1_out, and_2_out, and_3_out, and_4_out, and_5_out);
  Clock clock_1 (.out(clock_1_out));
  D_Flip_Flop d_ff_1 (.clk(clock_1_out), .D(or_2_out), .Q(d_ff_3_q[2]), .Qn(d_ff_1_qn));  // open: preset, en, reset
  D_Flip_Flop d_ff_2 (.clk(clock_1_out), .D(or_1_out), .Q(d_ff_3_q[1]), .Qn(d_ff_2_qn));  // open: preset, en, reset
  D_Flip_Flop d_ff_3 (.clk(clock_1_out), .D(d_ff_3_qn), .Q(d_ff_3_q[0]), .Qn(d_ff_3_qn));  // open: preset, en, reset
  // Probe on d_ff_3_q

  // Notes on the sheet:
  //   Q2'
  //   Q2
  //   Q0'
  //   Q0
  //   Q1'
  //   Q1
endmodule
