// Logisim project two 4-bit registers using MUX.circ as structural Verilog: 1 circuit, main circuit main
module main (
  input  [3:0] in_1,
  input  [3:0] in_2,
  input  in_3,
  output [3:0] out_4
);

  wire clock_1_out;
  wire [3:0] register_1_q, register_2_q;

  Clock clock_1 (.out(clock_1_out));
  Register #(.width(4)) register_1 (.D(in_1), .Q(register_1_q), .clk(clock_1_out));  // open: en, clr
  Register #(.width(4)) register_2 (.D(in_2), .Q(register_2_q), .clk(clock_1_out));  // open: en, clr
  Multiplexer #(.width(4), .disabled(0), .enable("false")) multiplexer_1 (
    .in0(register_1_q), .in1(register_2_q), .out(out_4), .sel(in_3));

  // Notes on the sheet:
  //   two 4-bit registers using MUX
endmodule
